# Fritzing sketch stepMotor (saved by Fritzing 0.9.0b)
circuit board: 5cm x 5cm
breadboards: 1

parts:
  VCC1 = Battery block 9V
  VCC2 = Battery block 9V
  IC1 = H-Bridge [package=THT]
  U3 = Voltage Regulator - 5V [package="TO220 [THT]"]
  M1 = Stepper Motor - Bipolar
  Y1 = Resonator [frequency="16 Mhz" package=THT]
  C1 = Electrolytic Capacitor [capacitance=10μF package="0605 [SMD, electrolytic]"]
  C2 = Capacitor [package=cap-pth-small2]
  U2 = atmega328 [package=dip]
  LED2 = smd LED [color="Red (633nm)" package="0603 [SMD]"]
  R1 = Resistor [tolerance=±5% resistance=220 package=THT]
  R2 = Resistor [tolerance=±5% resistance=220 package=THT]
  LED1 = smd LED [color="Red (633nm)" package="0603 [SMD]"]

nets (from the pcb view):
  GND: VCC1.-, VCC2.-, IC1.GND1, IC1.GND2, IC1.GND3, IC1.GND4, U3.GND, Y1.GND, C1.-, C2.2, U2.GND#7, LED2.cathode, R2.Pin_0
  N1: VCC1.+, VCC2.+, IC1.VCC2, U3.input_voltage, C2.1
  N2: IC1.1_2EN, IC1.3_4EN, IC1.VCC1, U3.output_voltage, C1.+, U2.VCC, R1.Pin_0
  N3: IC1.1A, U2.D8
  N4: IC1.1Y, M1.A
  N5: IC1.2Y, M1.C
  N6: IC1.2A, U2.D9_(PWM)
  N7: IC1.3A, U2.D10_(PWM)
  N8: IC1.3Y, M1.D
  N9: IC1.4Y, M1.B
  N10: IC1.4A, U2.D11_(PWM)
  N11: Y1.0, U2.XLAT1
  N12: Y1.pin_1, U2.XLAT2
  N13: U2.D13, LED1.anode
  N14: LED2.anode, R1.Pin_1
  N15: R2.Pin_1, LED1.cathode
